// Logisim project modulus.circ as structural Verilog
module _3bitModularCircuit (
  input  SA,
  input  A1,
  input  A0,
  input  SB,
  input  B1,
  input  B0,
  output SC,
  output C3,
  output C2,
  output C1,
  output C0,
  output Zero,
  output DivByZero
);

  wire and_1_out, and_2_out, and_3_out, and_4_out, and_5_out, and_6_out, and_7_out, and_8_out, and_9_out,
       and_10_out, and_11_out, and_12_out, and_13_out, and_14_out, and_15_out, and_16_out, and_17_out,
       and_19_out, and_20_out, and_21_out, not_1_out, not_2_out, not_3_out, not_4_out, not_5_out, not_6_out,
       not_7_out, not_8_out, not_9_out, not_10_out, not_11_out, or_1_out, or_2_out, or_3_out;

  not not_1 (not_1_out, A1);
  not not_2 (not_2_out, B0);
  not not_3 (not_3_out, A0);
  not not_4 (not_4_out, A1);
  not not_5 (not_5_out, A1);
  not not_6 (not_6_out, A0);
  not not_7 (not_7_out, A0);
  not not_8 (not_8_out, B0);
  and and_1 (and_1_out, A1, A0);
  nor nor_1 (DivByZero, B0, B1);
  and and_2 (and_2_out, SA, not_1_out);
  and and_3 (and_3_out, A0, B1);
  and and_4 (and_4_out, SA, A0);
  and and_5 (and_5_out, B1, not_2_out);
  and and_6 (and_6_out, SA, A1);
  not not_9 (not_9_out, A0);
  and and_7 (and_7_out, A1, not_3_out);
  and and_8 (and_8_out, B1, B0);
  and and_9 (and_9_out, not_4_out, A0);
  and and_10 (and_10_out, A0, B1);
  not not_10 (not_10_out, B0);
  and and_11 (and_11_out, not_5_out, not_6_out);
  and and_12 (and_12_out, not_7_out, not_8_out);
  not not_11 (not_11_out, B1);
  and and_13 (and_13_out, and_1_out, B0);
  and and_14 (and_14_out, and_2_out, and_3_out);
  and and_15 (and_15_out, and_4_out, and_5_out);
  and and_16 (and_16_out, and_6_out, not_9_out);
  and and_17 (and_17_out, B1, B0);
  and and_18 (C1, and_7_out, and_8_out);
  and and_19 (and_19_out, and_9_out, B1);
  and and_20 (and_20_out, and_10_out, not_10_out);
  or or_1 (or_1_out, and_11_out, and_12_out);
  or or_2 (or_2_out, not_11_out, and_13_out);
  or or_3 (or_3_out, and_14_out, and_15_out);
  and and_21 (and_21_out, and_16_out, and_17_out);
  or or_4 (C0, and_19_out, and_20_out);
  or or_5 (Zero, or_1_out, or_2_out);
  or or_6 (SC, or_3_out, and_21_out);

  assign C2 = 1'b0;
  assign C3 = 1'b0;
endmodule

module _3bitModularCircuit_NANDs (
  input  SA,
  input  A1,
  input  A0,
  input  SB,
  input  B1,
  input  B0,
  output SC,
  output C3,
  output C2,
  output C1,
  output C0,
  output Zero,
  output DivByZero
);

  wire nand_1_out, nand_2_out, nand_3_out, nand_4_out, nand_5_out, nand_6_out, nand_7_out, nand_8_out,
       nand_9_out, nand_10_out, nand_11_out, nand_12_out, nand_13_out, nand_14_out, nand_15_out, nand_16_out,
       nand_17_out, nand_18_out, nand_19_out, nand_20_out, nand_21_out, nand_22_out;

  nand nand_1 (nand_1_out, A1, A1);
  nand nand_2 (nand_2_out, B0, B0);
  nand nand_3 (nand_3_out, A0, A0);
  nand nand_4 (nand_4_out, A0, A0);
  nand nand_5 (nand_5_out, A1, A1);
  nand nand_6 (nand_6_out, B0, B0);
  nand nand_7 (nand_7_out, A1, A1);
  nand nand_8 (nand_8_out, A0, A0);
  nand nand_9 (nand_9_out, A0, A0);
  nand nand_10 (nand_10_out, B0, B0);
  nand nand_11 (nand_11_out, B0, B0);
  nand nand_12 (nand_12_out, B1, B1);
  nand nand_13 (nand_13_out, SA, nand_1_out, A0, B1);
  nand nand_14 (nand_14_out, SA, A0, B1, nand_2_out);
  nand nand_15 (nand_15_out, SA, A1, nand_3_out, B1, B0);
  nand nand_16 (nand_16_out, A1, nand_4_out, B1, B0);
  nand nand_17 (nand_17_out, nand_5_out, A0, B1);
  nand nand_18 (nand_18_out, A0, B1, nand_6_out);
  nand nand_19 (nand_19_out, nand_7_out, nand_8_out);
  nand nand_20 (nand_20_out, nand_9_out, nand_10_out);
  nand nand_21 (nand_21_out, A1, A0, B0);
  nand nand_22 (nand_22_out, nand_11_out, nand_12_out);
  nand nand_23 (SC, nand_13_out, nand_14_out, nand_15_out);
  nand nand_24 (C1, nand_16_out, nand_16_out);
  nand nand_25 (C0, nand_17_out, nand_18_out);
  nand nand_26 (Zero, nand_19_out, nand_20_out, B1, nand_21_out);
  nand nand_27 (DivByZero, nand_22_out, nand_22_out);

  assign C2 = 1'b0;
  assign C3 = 1'b0;
endmodule

module Simplified3BitModularCircuit (
  input  SA,
  input  A1,
  input  A0,
  input  SB,
  input  B1,
  input  B0,
  output SC,
  output C3,
  output C2,
  output C1,
  output C0,
  output DivByZero,
  output Zero
);

  wire nand_1_out, not_1_out, not_2_out;

  nor nor_1 (DivByZero, B0, B1);
  nand nand_1 (nand_1_out, A1, B0);
  not not_1 (not_1_out, A0);
  and and_1 (C0, A0, nand_1_out, B1);
  and and_2 (C1, not_1_out, A1, B1, B0);
  not not_2 (not_2_out, Zero);
  nor nor_2 (Zero, C0, C1);
  and and_3 (SC, SA, not_2_out);

  assign C2 = 1'b0;
  assign C3 = 1'b0;
endmodule
