// Logisim project multiplier finial circuit.circ as structural Verilog
module main (
  input  a1,
  input  a2,
  input  a3,
  input  b1,
  input  b2,
  input  b3,
  input  in_7,
  input  in_8,
  output s1,
  output s2,
  output s3,
  output Zero_flag,
  output Sign_flag
);

  wire and_1_out, and_2_out, and_3_out, and_4_out, and_5_out, and_6_out, and_7_out, fall_adder_1_fcarry,
       fall_adder_1_fsum, fall_adder_2_fcarry, fall_adder_2_fsum, half_adder_1_carry, half_adder_1_sum,
       half_adder_2_carry, half_adder_3_carry, not_1_out, not_2_out, or_1_out, xor_1_out, xor_2_out,
       xor_3_out, xor_4_out, xor_5_out, xor_6_out, xor_7_out, xor_8_out, xor_9_out, xor_10_out;

  not not_1 (not_1_out, in_8);
  xor xor_1 (xor_1_out, b3, and_1_out);
  and and_1 (and_1_out, in_7, not_1_out);
  xor xor_2 (xor_2_out, xor_1_out, a3);
  and and_2 (and_2_out, xor_2_out, a3);
  and and_3 (and_3_out, xor_2_out, xor_1_out);
  and and_4 (and_4_out, xor_2_out, a3);
  and and_5 (and_5_out, xor_2_out, xor_1_out);
  xor xor_3 (xor_3_out, a1, and_2_out);
  xor xor_4 (xor_4_out, b1, and_3_out);
  xor xor_5 (xor_5_out, a2, and_4_out);
  xor xor_6 (xor_6_out, b2, and_5_out);
  Half_Adder half_adder_1 (.in_1(xor_3_out), .in_2(xor_4_out), .carry(half_adder_1_carry), .sum(half_adder_1_sum));
  Fall_Adder fall_adder_1 (
    .in_1(half_adder_1_carry), .in_2(xor_5_out), .in_3(xor_6_out), .FCarry(fall_adder_1_fcarry),
    .FSum(fall_adder_1_fsum));
  Fall_Adder fall_adder_2 (
    .in_1(fall_adder_1_fcarry), .in_2(a3), .in_3(xor_1_out), .FCarry(fall_adder_2_fcarry),
    .FSum(fall_adder_2_fsum));
  xor xor_7 (xor_7_out, xor_2_out, fall_adder_2_fcarry);
  not not_2 (not_2_out, fall_adder_2_fcarry);
  and and_6 (and_6_out, not_2_out, xor_2_out);
  and and_7 (and_7_out, fall_adder_2_fcarry, xor_2_out);
  xor xor_8 (xor_8_out, and_6_out, half_adder_1_sum);
  xor xor_9 (xor_9_out, and_6_out, fall_adder_1_fsum);
  xor xor_10 (xor_10_out, and_6_out, fall_adder_2_fsum);
  and and_8 (Sign_flag, xor_7_out, or_1_out);
  Half_Adder half_adder_2 (.in_1(and_7_out), .in_2(xor_8_out), .carry(half_adder_2_carry), .sum(s1));
  Half_Adder half_adder_3 (.in_1(half_adder_2_carry), .in_2(xor_9_out), .carry(half_adder_3_carry), .sum(s2));
  xor xor_11 (s3, half_adder_3_carry, xor_10_out);
  not not_3 (Zero_flag, or_1_out);
  or or_1 (or_1_out, s3, s2, s1);
endmodule

module half_adder (
  input  in_1,
  input  in_2,
  output out_3,
  output out_4
);

  xor xor_1 (out_3, in_1, in_2);
  and and_1 (out_4, in_1, in_2);
endmodule

module MULTIPLIER (
  input  A0,
  input  A1,
  input  A3,
  input  B0,
  input  B1,
  input  B3,
  output sign,
  output zero
);

  wire and_1_out, and_2_out, and_3_out, and_4_out, half_adder_1_out_3, half_adder_1_out_4,
       half_adder_2_out_3, half_adder_2_out_4, n7448_1_p10, n7448_1_p11, n7448_1_p12, n7448_1_p13,
       n7448_1_p14, n7448_1_p15, n7448_1_p16, n7448_2_p10, n7448_2_p11, n7448_2_p12, n7448_2_p13,
       n7448_2_p14, n7448_2_p15, n7448_2_p16, or_1_out;

  xor xor_1 (sign, A3, B3);
  and and_1 (and_1_out, A0, B1);
  and and_2 (and_2_out, A1, B1);
  and and_3 (and_3_out, A0, B0);
  and and_4 (and_4_out, A1, B0);
  half_adder half_adder_1 (.in_1(and_4_out), .in_2(and_1_out), .out_3(half_adder_1_out_3), .out_4(half_adder_1_out_4));
  half_adder half_adder_2 (
    .in_1(half_adder_1_out_4), .in_2(and_2_out), .out_3(half_adder_2_out_3), .out_4(half_adder_2_out_4));
  or or_1 (or_1_out, and_3_out, half_adder_1_out_3, half_adder_2_out_3, half_adder_2_out_4);
  not not_1 (zero, or_1_out);
  // _7448 7448_1: pin names not known; wires that end beside it: half_adder_1_out_3, half_adder_2_out_3, 1'b1, 1'b1, 1'b1, half_adder_2_out_4, and_3_out, 1'b0, 1'b1, n7448_1_p10, n7448_1_p11, n7448_1_p12, n7448_1_p13, n7448_1_p14, n7448_1_p15, n7448_1_p16
  // _7448 7448_2: pin names not known; wires that end beside it: 1'b0, 1'b0, 1'b1, 1'b1, 1'b1, 1'b0, sign, 1'b0, 1'b1, n7448_2_p10, n7448_2_p11, n7448_2_p12, n7448_2_p13, n7448_2_p14, n7448_2_p15, n7448_2_p16
  _7_Segment_Display u_7_segment_display_1 (
    .g(n7448_2_p11), .f(n7448_2_p10), .a(n7448_2_p12), .b(n7448_2_p13), .e(n7448_2_p16), .d(n7448_2_p15),
    .c(n7448_2_p14));  // open: dp
  _7_Segment_Display u_7_segment_display_2 (
    .g(n7448_1_p11), .f(n7448_1_p10), .a(n7448_1_p12), .b(n7448_1_p13), .e(n7448_1_p16), .d(n7448_1_p15),
    .c(n7448_1_p14));  // open: dp

  // Notes on the sheet:
  //   c0
  //   c1
  //   c2
  //   c3
endmodule

module full_adder (
  input  in_1,
  input  in_2,
  input  in_3,
  output out_4,
  output out_5
);

  wire half_adder_1_out_3, half_adder_1_out_4, half_adder_2_out_4;

  half_adder half_adder_1 (.in_1(in_1), .in_2(in_2), .out_3(half_adder_1_out_3), .out_4(half_adder_1_out_4));
  half_adder half_adder_2 (.in_1(half_adder_1_out_3), .in_2(in_3), .out_3(out_4), .out_4(half_adder_2_out_4));
  or or_1 (out_5, half_adder_1_out_4, half_adder_2_out_4);
endmodule

module adder_subtractor (
  input  a1,
  input  a2,
  input  a3,
  input  b1,
  input  b2,
  input  b3,
  input  in_7,
  input  in_8,
  output s1,
  output s2,
  output s3,
  output Zero_flag,
  output Sign_flag
);

  wire and_1_out, and_2_out, and_3_out, and_4_out, and_5_out, and_6_out, and_7_out, fall_adder_1_fcarry,
       fall_adder_1_fsum, fall_adder_2_fcarry, fall_adder_2_fsum, half_adder_1_carry, half_adder_1_sum,
       half_adder_2_carry, half_adder_3_carry, not_1_out, not_2_out, or_1_out, xor_1_out, xor_2_out,
       xor_3_out, xor_4_out, xor_5_out, xor_6_out, xor_7_out, xor_8_out, xor_9_out, xor_10_out;

  not not_1 (not_1_out, in_8);
  xor xor_1 (xor_1_out, b3, and_1_out);
  and and_1 (and_1_out, in_7, not_1_out);
  xor xor_2 (xor_2_out, xor_1_out, a3);
  and and_2 (and_2_out, xor_2_out, a3);
  and and_3 (and_3_out, xor_2_out, xor_1_out);
  and and_4 (and_4_out, xor_2_out, a3);
  and and_5 (and_5_out, xor_2_out, xor_1_out);
  xor xor_3 (xor_3_out, a1, and_2_out);
  xor xor_4 (xor_4_out, b1, and_3_out);
  xor xor_5 (xor_5_out, a2, and_4_out);
  xor xor_6 (xor_6_out, b2, and_5_out);
  Half_Adder half_adder_1 (.in_1(xor_3_out), .in_2(xor_4_out), .carry(half_adder_1_carry), .sum(half_adder_1_sum));
  Fall_Adder fall_adder_1 (
    .in_1(half_adder_1_carry), .in_2(xor_5_out), .in_3(xor_6_out), .FCarry(fall_adder_1_fcarry),
    .FSum(fall_adder_1_fsum));
  Fall_Adder fall_adder_2 (
    .in_1(fall_adder_1_fcarry), .in_2(a3), .in_3(xor_1_out), .FCarry(fall_adder_2_fcarry),
    .FSum(fall_adder_2_fsum));
  xor xor_7 (xor_7_out, xor_2_out, fall_adder_2_fcarry);
  not not_2 (not_2_out, fall_adder_2_fcarry);
  and and_6 (and_6_out, not_2_out, xor_2_out);
  and and_7 (and_7_out, fall_adder_2_fcarry, xor_2_out);
  xor xor_8 (xor_8_out, and_6_out, half_adder_1_sum);
  xor xor_9 (xor_9_out, and_6_out, fall_adder_1_fsum);
  xor xor_10 (xor_10_out, and_6_out, fall_adder_2_fsum);
  and and_8 (Sign_flag, xor_7_out, or_1_out);
  Half_Adder half_adder_2 (.in_1(and_7_out), .in_2(xor_8_out), .carry(half_adder_2_carry), .sum(s1));
  Half_Adder half_adder_3 (.in_1(half_adder_2_carry), .in_2(xor_9_out), .carry(half_adder_3_carry), .sum(s2));
  xor xor_11 (s3, half_adder_3_carry, xor_10_out);
  not not_3 (Zero_flag, or_1_out);
  or or_1 (or_1_out, s3, s2, s1);
endmodule
