// Logisim project multiplier.circ as structural Verilog
module half_adder (
  input  in_1,
  input  in_2,
  output out_3,
  output out_4
);

  xor xor_1 (out_3, in_1, in_2);
  and and_1 (out_4, in_1, in_2);
endmodule

module MULTIPLIER (
  input  A0,
  input  A1,
  input  A3,
  input  B0,
  input  B1,
  input  B3,
  output C0,
  output C1,
  output C2,
  output C3,
  output C4
);

  wire and_2_out, and_3_out, and_4_out, half_adder_1_out_4;

  and and_1 (C0, A0, B0);
  and and_2 (and_2_out, A1, B0);
  and and_3 (and_3_out, A0, B1);
  and and_4 (and_4_out, A1, B1);
  xor xor_1 (C4, A3, B3);
  half_adder half_adder_1 (.in_1(and_2_out), .in_2(and_3_out), .out_3(C1), .out_4(half_adder_1_out_4));
  half_adder half_adder_2 (.in_1(half_adder_1_out_4), .in_2(and_4_out), .out_3(C2), .out_4(C3));
endmodule

module full_adder (
  input  in_1,
  input  in_2,
  input  in_3,
  output out_4,
  output out_5
);

  wire half_adder_1_out_3, half_adder_1_out_4, half_adder_2_out_4;

  half_adder half_adder_1 (.in_1(in_1), .in_2(in_2), .out_3(half_adder_1_out_3), .out_4(half_adder_1_out_4));
  half_adder half_adder_2 (.in_1(half_adder_1_out_3), .in_2(in_3), .out_3(out_4), .out_4(half_adder_2_out_4));
  or or_1 (out_5, half_adder_1_out_4, half_adder_2_out_4);
endmodule
