// Logisim project project initial.circ as structural Verilog
module Half_Adder (
  input  in_1,
  input  in_2,
  output carry,
  output sum
);

  and and_1 (carry, in_1, in_2);
  xor xor_1 (sum, in_1, in_2);
endmodule

module Fall_Adder (
  input  in_1,
  input  in_2,
  input  in_3,
  output FCarry,
  output FSum
);

  wire and_1_out, and_2_out, xor_1_out;

  and and_1 (and_1_out, in_1, in_2);
  xor xor_1 (xor_1_out, in_1, in_2);
  and and_2 (and_2_out, xor_1_out, in_3);
  xor xor_2 (FSum, xor_1_out, in_3);
  or or_1 (FCarry, and_1_out, and_2_out);
endmodule

module adder_subtractor (
  input  A0,
  input  A1,
  input  SA,
  input  B0,
  input  B1,
  input  SB,
  input  [1:0] in_7,
  output SS0,
  output SS1,
  output SS2,
  output Sign_flag
);

  wire and_1_out, and_2_out, and_3_out, and_4_out, and_5_out, and_6_out, demultiplexer_1_out1,
       fall_adder_1_fcarry, fall_adder_1_fsum, fall_adder_2_fcarry, fall_adder_2_fsum, half_adder_1_carry,
       half_adder_1_sum, half_adder_2_carry, half_adder_3_carry, not_1_out, or_1_out, xor_1_out, xor_2_out,
       xor_3_out, xor_4_out, xor_5_out, xor_6_out, xor_7_out, xor_8_out, xor_9_out, xor_10_out;

  Demultiplexer #(.select(2)) demultiplexer_1 (
    .out1(demultiplexer_1_out1), .in(1'b1), .sel(in_7));  // open: out0, out2, out3, en
  xor xor_1 (xor_1_out, SB, demultiplexer_1_out1);
  xor xor_2 (xor_2_out, xor_1_out, SA);
  and and_1 (and_1_out, xor_2_out, SA);
  and and_2 (and_2_out, xor_2_out, xor_1_out);
  and and_3 (and_3_out, xor_2_out, SA);
  and and_4 (and_4_out, xor_2_out, xor_1_out);
  xor xor_3 (xor_3_out, A0, and_1_out);
  xor xor_4 (xor_4_out, B0, and_2_out);
  xor xor_5 (xor_5_out, A1, and_3_out);
  xor xor_6 (xor_6_out, B1, and_4_out);
  Half_Adder half_adder_1 (.in_1(xor_3_out), .in_2(xor_4_out), .carry(half_adder_1_carry), .sum(half_adder_1_sum));
  Fall_Adder fall_adder_1 (
    .in_1(half_adder_1_carry), .in_2(xor_5_out), .in_3(xor_6_out), .FCarry(fall_adder_1_fcarry),
    .FSum(fall_adder_1_fsum));
  Fall_Adder fall_adder_2 (
    .in_1(fall_adder_1_fcarry), .in_2(SA), .in_3(xor_1_out), .FCarry(fall_adder_2_fcarry),
    .FSum(fall_adder_2_fsum));
  xor xor_7 (xor_7_out, xor_2_out, fall_adder_2_fcarry);
  not not_1 (not_1_out, fall_adder_2_fcarry);
  and and_5 (and_5_out, not_1_out, xor_2_out);
  and and_6 (and_6_out, fall_adder_2_fcarry, xor_2_out);
  xor xor_8 (xor_8_out, and_5_out, half_adder_1_sum);
  xor xor_9 (xor_9_out, and_5_out, fall_adder_1_fsum);
  xor xor_10 (xor_10_out, and_5_out, fall_adder_2_fsum);
  and and_7 (Sign_flag, xor_7_out, or_1_out);
  Half_Adder half_adder_2 (.in_1(and_6_out), .in_2(xor_8_out), .carry(half_adder_2_carry), .sum(SS0));
  Half_Adder half_adder_3 (.in_1(half_adder_2_carry), .in_2(xor_9_out), .carry(half_adder_3_carry), .sum(SS1));
  xor xor_11 (SS2, half_adder_3_carry, xor_10_out);
  or or_1 (or_1_out, SS2, SS1, SS0);
endmodule

module modulor (
  input  SA,
  input  A1,
  input  A0,
  input  SB,
  input  B1,
  input  B0,
  output SC,
  output C1,
  output C0,
  output DivByZero
);

  wire nand_1_out, nor_2_out, not_1_out, not_2_out;

  nor nor_1 (DivByZero, B0, B1);
  nand nand_1 (nand_1_out, A1, B0);
  not not_1 (not_1_out, A0);
  and and_1 (C0, A0, nand_1_out, B1);
  and and_2 (C1, not_1_out, A1, B1, B0);
  not not_2 (not_2_out, nor_2_out);
  nor nor_2 (nor_2_out, C0, C1);
  and and_3 (SC, SA, not_2_out);
endmodule

module multipluer (
  input  a0,
  input  a1,
  input  sa,
  input  b0,
  input  b1,
  input  sb,
  output m0,
  output m1,
  output m2,
  output m4,
  output sm
);

  wire and_1_out, and_2_out, and_4_out, half_adder_1_out_4, or_1_out, xor_1_out;

  xor xor_1 (xor_1_out, sa, sb);
  and and_1 (and_1_out, a0, b1);
  and and_2 (and_2_out, a1, b1);
  and and_3 (m0, a0, b0);
  and and_4 (and_4_out, a1, b0);
  half_adder half_adder_1 (.in_1(and_4_out), .in_2(and_1_out), .out_3(m1), .out_4(half_adder_1_out_4));
  half_adder half_adder_2 (.in_1(half_adder_1_out_4), .in_2(and_2_out), .out_3(m2), .out_4(m4));
  or or_1 (or_1_out, m0, m1, m2, m4);
  and and_5 (sm, xor_1_out, or_1_out);

  // Notes on the sheet:
  //   A0
  //   A1
  //   A3
  //   B0
  //   B1
  //   B3
  //   c0
  //   c1
  //   c2
  //   c3
endmodule

module finalCircuit (
  input  SB,
  input  B1,
  input  B0,
  input  SA,
  input  A1,
  input  A0,
  input  [1:0] mode1
);

  wire adder_subtractor_1_sign_flag, adder_subtractor_1_ss0, adder_subtractor_1_ss1, adder_subtractor_1_ss2,
       and_1_out, demultiplexer_1_out3, modulor_1_c0, modulor_1_c1, modulor_1_divbyzero, modulor_1_sc,
       multiplexer_1_out, multiplexer_2_out, multiplexer_3_out, multiplexer_4_out, multiplexer_5_out,
       multipluer_1_m0, multipluer_1_m1, multipluer_1_m2, multipluer_1_m4, multipluer_1_sm, n7448_1_p10,
       n7448_1_p11, n7448_1_p12, n7448_1_p13, n7448_1_p14, n7448_1_p15, n7448_1_p16, nor_1_out;

  Demultiplexer #(.select(2)) demultiplexer_1 (
    .out3(demultiplexer_1_out3), .in(1'b1), .sel(mode1));  // open: out0, out1, out2, en
  adder_subtractor adder_subtractor_1 (
    .A0(A0), .A1(A1), .SA(SA), .B0(B0), .B1(B1), .SB(SB), .in_7(mode1), .SS0(adder_subtractor_1_ss0),
    .SS1(adder_subtractor_1_ss1), .SS2(adder_subtractor_1_ss2), .Sign_flag(adder_subtractor_1_sign_flag));
  multipluer multipluer_1 (
    .a0(A0), .a1(A1), .sa(SA), .b0(B0), .b1(B1), .sb(SB), .m0(multipluer_1_m0), .m1(multipluer_1_m1),
    .m2(multipluer_1_m2), .m4(multipluer_1_m4), .sm(multipluer_1_sm));
  modulor modulor_1 (
    .SA(SA), .A1(A1), .A0(A0), .SB(SB), .B1(B1), .B0(B0), .DivByZero(modulor_1_divbyzero), .SC(modulor_1_sc),
    .C1(modulor_1_c1), .C0(modulor_1_c0));
  Multiplexer #(.select(2)) multiplexer_1 (
    .in0(adder_subtractor_1_ss0), .in1(adder_subtractor_1_ss0), .in2(multipluer_1_m0), .in3(modulor_1_c0),
    .out(multiplexer_1_out), .sel(mode1));  // open: en
  Multiplexer #(.select(2)) multiplexer_2 (
    .in0(adder_subtractor_1_ss1), .in1(adder_subtractor_1_ss1), .in2(multipluer_1_m1), .in3(modulor_1_c1),
    .out(multiplexer_2_out), .sel(mode1));  // open: en
  Multiplexer #(.select(2)) multiplexer_3 (
    .in0(adder_subtractor_1_ss2), .in1(adder_subtractor_1_ss2), .in2(multipluer_1_m2), .in3(1'b0),
    .out(multiplexer_3_out), .sel(mode1));  // open: en
  Multiplexer #(.select(2)) multiplexer_4 (
    .in0(1'b0), .in1(1'b0), .in2(multipluer_1_m4), .in3(1'b0), .out(multiplexer_4_out), .sel(mode1));  // open: en
  Multiplexer #(.select(2)) multiplexer_5 (
    .in0(adder_subtractor_1_sign_flag), .in1(adder_subtractor_1_sign_flag), .in2(multipluer_1_sm),
    .in3(modulor_1_sc), .out(multiplexer_5_out), .sel(mode1));  // open: en
  nor nor_1 (nor_1_out, multiplexer_4_out, multiplexer_3_out, multiplexer_2_out, multiplexer_1_out);
  and and_1 (and_1_out, modulor_1_divbyzero, demultiplexer_1_out3);
  // _7448 7448_1: pin names not known; wires that end beside it: multiplexer_2_out, multiplexer_3_out, 1'b1, 1'b1, 1'b1, multiplexer_4_out, multiplexer_1_out, 1'b0, 1'b1, n7448_1_p10, n7448_1_p11, n7448_1_p12, n7448_1_p13, n7448_1_p14, n7448_1_p15, n7448_1_p16
  LED Sign (.in(multiplexer_5_out));
  LED DivByZero (.in(and_1_out));
  LED Zero (.in(nor_1_out));
  _7_Segment_Display u_7_segment_display_1 (
    .g(multiplexer_5_out), .f(1'b0), .a(1'b0), .b(1'b0), .e(1'b0), .d(1'b0), .c(1'b0), .dp(1'b0));
  _7_Segment_Display u_7_segment_display_2 (
    .g(n7448_1_p11), .f(n7448_1_p10), .a(n7448_1_p12), .b(n7448_1_p13), .e(n7448_1_p16), .d(n7448_1_p15),
    .c(n7448_1_p14));  // open: dp
endmodule
